# Fritzing sketch two_display_demo (saved by Fritzing 0.9.2b)
breadboards: 1

parts:
  WeMos_D1_Mini1 = WeMos D1 Mini
  Squix1 = OLED 0.96" 128x64 I2C SSD1306
  Squix2 = OLED 0.96" 128x64 I2C SSD1306

nets:
  VCC: WeMos_D1_Mini1.3V3, Squix1.VCC, Squix2.VCC
  N1: WeMos_D1_Mini1.D1, Squix1.SCL, Squix2.SCL
  N2: WeMos_D1_Mini1.D2, Squix1.SCA
  N3: WeMos_D1_Mini1.D3, Squix2.SCA
  GND: WeMos_D1_Mini1.G, Squix1.GND, Squix2.GND
